# Fritzing sketch Khang (saved by Fritzing 0.9.1b)
breadboards: 1

parts:
  Part1 = Arduino Uno (Rev3)
  S1 = Momentary Switch [package=ksa_sealed_tac_switch]
  BAT1 = BC9VPC [package=bc9vpc]
  Q1 = Basic FET N-Channel [package="DPak [SMD]"]
  R1 = Resistor [package="2512 [SMD]"]
  L1 = Solenoid
  D1 = Diode [package=diode-hv]

nets:
  N1: Part1.D2, Q1.source
  N2: Part1.D7, S1.1
  N3: Part1.5V, S1.4
  N4: Part1.GND, BAT1.V-, Q1.Gate, R1.Pin_0, D1.C
  N5: S1.2, R1.Pin_1
  N6: BAT1.V+, L1.pin1
  N7: Q1.drain, L1.pin2, D1.A
